# Fritzing sketch airpi (saved by Fritzing 0.9.0b)
circuit board: 3.8cm x 3cm
breadboards: 1

parts:
  BME280 = BME280 Pressure and Humidity Sensor Breakout
  DS3231_RTC = DS3231 AT24C32 Real Time Clock
  PMS5003 = Plantower PMS5003
  Raspberry_Pi = Raspberry Pi B rev1

nets:
  5V: BME280.5V, PMS5003.VCC, Raspberry_Pi.5V
  GND: BME280.GND, DS3231_RTC.GND, PMS5003.GND, Raspberry_Pi.GND
  N1: BME280.SDI, DS3231_RTC.SDA, Raspberry_Pi.GIPO_0
  N2: BME280.SCK, DS3231_RTC.SCL, Raspberry_Pi.GIPO_1
  VCC: DS3231_RTC.VCC, Raspberry_Pi.3V3
  N3: PMS5003.RXD, Raspberry_Pi.GPIO_14
  N4: PMS5003.TXD, Raspberry_Pi.GPIO_15
  N5: PMS5003.RESET, Raspberry_Pi.GPIO_17

custom parts:
  BME280 Pressure and Humidity Sensor Breakout: The BME280 is as combined digital humidity, pressure and temperature sensor proven sensing principles. The sensor provides both SPI and I2C interfaces. The 7-bit device address is 111011x. The 6 MSB bits are fixed. The last bit is changeable by SDO value and can be changed during operation. Connecting SDO to GND results in slave address 1110110 (0x76); connection it to VDDIO results in slave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
  DS3231 AT24C32 Real Time Clock: Real-time clock chip: DS3231, Memory chip: AT24C32 (32 Kb storage capacity), On-chip temperature sensor with an accuracy of ±3 ℃, I2C bus interface maximum speed: 400 kHz. Operating voltage: 3.3 V to 5.5 V and it also features battery backup capabilities.
  Plantower PMS5003: Particulate Matter Sensor
  Raspberry Pi B rev1: The awesome Raspberry Pi ARM Board
